# Fritzing sketch fritzing (saved by Fritzing 0.9.3b)

parts:
  Part1 = Arduino Uno (Rev3) - ICSP
  Part2 = MQ-4
  U1 = 2-Channel 5v Relay Shield [package=relay-2ch5v10a]
  DHT1 = DHT11 Humitidy and Temperature Sensor

nets:
  N1: Part1.A0, Part2.DO
  N2: Part1.D3_PWM, DHT1.DATA
  N3: Part1.D4, U1.IN1
  5V: Part1.5V, DHT1.VDD
  N4: Part1.GND, DHT1.NULL

notes:
  SIM808 GPS/GPRS/GSM Shield
  3-wire Serial LCD Module

custom parts:
  2-Channel 5v Relay Shield: 2 Channel 5v Relay Shield w. 2x SPD-06VDC-SD-C
  DHT11 Humitidy and Temperature Sensor: DHT11 Humidity and Temperature Sensor
